# Fritzing sketch circuit robotics (saved by Fritzing 0.9.3b)
breadboards: 1

parts:
  Part1 = Arduino Uno (Rev3) - ICSP
  J1 = Basic Servo
  J2 = Basic Servo
  J5 = Basic Servo
  J3 = Basic Servo

nets:
  N1: Part1.D9_PWM, J2.pulse
  N2: Part1.D10_PWM/SS, J1.pulse
  N3: Part1.D5_PWM, J5.pulse
  N4: Part1.D6_PWM, J3.pulse
  VCC: Part1.5V, J1.vcc, J2.vcc, J5.vcc, J3.vcc
  GND: Part1.GND, J1.gnd, J2.gnd, J5.gnd, J3.gnd

notes:
  Yellow --- signal
  Red --- vcc
  Black --- Ground
